# Fritzing sketch rescueMe (saved by Fritzing 0.9.3b)
breadboards: 1

parts:
  Part1 = Photon
  Part2 = Breakout Board for Electret Microphone
  PIR = HC-SR501 Body Sensor Module
  J1 = Basic Servo
  VCC1 = Battery  # not connected

nets:
  N1: Part1.A5, Part2.AUD
  GND: Part1.GND, Part2.GND, PIR.GND, J1.gnd
  N2: Part1.D1, PIR.OUT, J1.pulse
  VCC: Part1.3V3, Part2.VCC, PIR.VCC

custom parts:
  HC-SR501 Body Sensor Module: Pyroelectric Infrared PIR Motion Sensor Detector Module
